# Fritzing sketch rangkaianswitch (saved by Fritzing 0.9.4)
breadboards: 1

parts:
  R1 = Resistor [tolerance=±5% resistance=560 package=THT]
  Q1 = PNP-Transistor [part_number=9015 package="TO92 [THT]"]
  R2 = Resistor [tolerance=±5% resistance=560 package=THT]
  M1 = fc-51 [package=THT]

nets:
  Sensor: R1.Pin_0, M1.pin1
  N1: R1.Pin_1, Q1.B
  5V: Q1.E, M1.pin3
  ke mesin: Q1.C, R2.Pin_0
  GND: R2.Pin_1, M1.pin2
