# Fritzing sketch wastafel (saved by Fritzing 0.9.4)
breadboards: 1

parts:
  Part1 = Arduino Nano (Rev3.0) (ICSP)
  Part2 = JTRON 1CH RELAY
  Part3 = SRF05 Ultrasonic Rangefinder

nets:
  GND: Part1.GND, Part2.connector5, Part3.GND
  N1: Part1.D2, Part3.Trig
  N2: Part1.D4, Part3.Echo
  N3: Part1.D6, Part2.connector4
  5V: Part1.5V, Part2.connector0, Part3.VCC
